// Logisim project control_logic.circ as structural Verilog: 1 circuit, main circuit control_logic
module control_logic (
  input  [31:0] inst,
  input  BrEq,
  input  BrLt,
  output [3:0] MemW_en,
  output [1:0] MemR_en,
  output KILL_INST,
  output PCSel,
  output RegWEn,
  output [2:0] ImmSel,
  output BrUn,
  output ASel,
  output BSel,
  output [3:0] ALUSel,
  output MemRW,
  output [1:0] WBSel,
  output CSRSel,
  output CSRWen
);

  wire add0, and1, and_1_out, and_2_out, and_3_out, and_4_out, and_5_out, and_6_out, and_7_out, and_8_out,
       and_9_out, and_21_out, and_22_out, bsel13, comparator_1_eq, comparator_2_eq, comparator_3_eq,
       comparator_4_eq, comparator_5_eq, comparator_6_eq, comparator_7_eq, comparator_8_eq, comparator_9_eq,
       comparator_10_eq, comparator_11_eq, comparator_12_eq, funct7_zero, is_auipc, is_I, is_I_ar, is_I_jalr,
       is_I_load, is_R, is_S, is_SB, is_U, is_UJ, mul10, mulh14, mulhu11, multiplexer_3_out, not_1_out,
       not_2_out, not_3_out, or2, or_2_out, or_3_out, or_4_out, or_5_out, or_6_out, or_7_out, or_8_out,
       or_13_out, sll6, slt7, sra5, srl4, sub12, xor3;
  wire [1:0] bit_extender_1_out, multiplexer_17_out, multiplexer_20_out;
  wire [2:0] multiplexer_1_out, multiplexer_2_out, multiplexer_4_out, multiplexer_5_out, multiplexer_6_out;
  wire [3:0] multiplexer_8_out, multiplexer_9_out, multiplexer_10_out, multiplexer_11_out,
       multiplexer_12_out, multiplexer_13_out, multiplexer_14_out, multiplexer_15_out, multiplexer_18_out,
       multiplexer_19_out, multiplexer_21_out, multiplexer_23_out;

  Comparator #(.width(3)) comparator_1 (.a(inst[14:12]), .b(3'b000), .eq(comparator_1_eq));  // open: gt, lt
  and and_1 (and_1_out, is_R, funct7_zero);
  and and_2 (and_2_out, is_R, funct7_zero);
  and and_3 (and_3_out, is_R, funct7_zero);
  and and_4 (and_4_out, is_R, funct7_zero);
  and and_5 (and_5_out, is_R, inst[30]);
  and and_6 (and_6_out, is_R, funct7_zero);
  and and_7 (and_7_out, is_R, funct7_zero);
  Comparator #(.width(3)) comparator_2 (.a(inst[14:12]), .b(3'b000), .eq(comparator_2_eq));  // open: gt, lt
  Comparator #(.width(3)) comparator_3 (.a(inst[14:12]), .b(3'b001), .eq(comparator_3_eq));  // open: gt, lt
  or or_1 (is_U, is_auipc, bsel13);
  and and_8 (and_8_out, is_I_ar, comparator_1_eq);
  Comparator #(.width(3)) comparator_4 (.a(inst[14:12]), .b(3'b111), .eq(comparator_4_eq));  // open: gt, lt
  or or_2 (or_2_out, and_1_out, is_I_ar);
  Comparator #(.width(3)) comparator_5 (.a(inst[14:12]), .b(3'b110), .eq(comparator_5_eq));  // open: gt, lt
  or or_3 (or_3_out, and_2_out, is_I_ar);
  Comparator #(.width(3)) comparator_6 (.a(inst[14:12]), .b(3'b100), .eq(comparator_6_eq));  // open: gt, lt
  or or_4 (or_4_out, and_3_out, is_I_ar);
  Comparator #(.width(3)) comparator_7 (.a(inst[14:12]), .b(3'b101), .eq(comparator_7_eq));  // open: gt, lt
  not not_1 (not_1_out, inst[30]);
  or or_5 (or_5_out, and_4_out, is_I_ar);
  Comparator #(.width(3)) comparator_8 (.a(inst[14:12]), .b(3'b101), .eq(comparator_8_eq));  // open: gt, lt
  or or_6 (or_6_out, and_5_out, is_I_ar);
  Comparator #(.width(3)) comparator_9 (.a(inst[14:12]), .b(3'b001), .eq(comparator_9_eq));  // open: gt, lt
  or or_7 (or_7_out, and_6_out, is_I_ar);
  Comparator #(.width(3)) comparator_10 (.a(inst[14:12]), .b(3'b010), .eq(comparator_10_eq));  // open: gt, lt
  or or_8 (or_8_out, and_7_out, is_I_ar);
  Comparator #(.width(3)) comparator_11 (.a(inst[14:12]), .b(3'b000), .eq(comparator_11_eq));  // open: gt, lt
  Comparator #(.width(3)) comparator_12 (.a(inst[14:12]), .b(3'b011), .eq(comparator_12_eq));  // open: gt, lt
  Comparator #(.mode("unsigned"), .width(5)) comparator_13 (.a(inst[6:2]), .b(5'b01100), .eq(is_R));  // open: gt, lt
  Comparator #(.mode("unsigned"), .width(5)) comparator_14 (
    .a(inst[6:2]), .b({5{1'b0}}), .eq(is_I_load));  // open: gt, lt
  Comparator #(.mode("unsigned"), .width(5)) comparator_15 (.a(inst[6:2]), .b(5'b00100), .eq(is_I_ar));  // open: gt, lt
  Comparator #(.mode("unsigned"), .width(5)) comparator_16 (
    .a(inst[6:2]), .b(5'b11001), .eq(is_I_jalr));  // open: gt, lt
  Comparator #(.mode("unsigned"), .width(5)) comparator_17 (.a(inst[6:2]), .b(5'b11100), .eq(CSRWen));  // open: gt, lt
  or or_9 (is_I, is_I_load, is_I_ar, is_I_jalr, CSRWen);
  Comparator #(.mode("unsigned"), .width(5)) comparator_18 (.a(inst[6:2]), .b(5'b01000), .eq(is_S));  // open: gt, lt
  Comparator #(.mode("unsigned"), .width(5)) comparator_19 (.a(inst[6:2]), .b(5'b11000), .eq(is_SB));  // open: gt, lt
  Comparator #(.mode("unsigned"), .width(5)) comparator_20 (
    .a(inst[6:2]), .b(5'b00101), .eq(is_auipc));  // open: gt, lt
  Comparator #(.mode("unsigned"), .width(5)) comparator_21 (.a(inst[6:2]), .b(5'b01101), .eq(bsel13));  // open: gt, lt
  Comparator #(.mode("unsigned"), .width(5)) comparator_22 (.a(inst[6:2]), .b(5'b11011), .eq(is_UJ));  // open: gt, lt
  and and_9 (and_9_out, comparator_1_eq, funct7_zero);
  and and_10 (and1, comparator_4_eq, or_2_out);
  and and_11 (or2, comparator_5_eq, or_3_out);
  and and_12 (xor3, comparator_6_eq, or_4_out);
  and and_13 (srl4, comparator_7_eq, not_1_out, or_5_out);
  and and_14 (sll6, comparator_9_eq, or_7_out);
  and and_15 (slt7, comparator_10_eq, or_8_out);
  and and_16 (mul10, comparator_11_eq, inst[25], is_R);
  and and_17 (mulhu11, comparator_12_eq, inst[25], is_R);
  and and_18 (sub12, is_R, comparator_2_eq, inst[30]);
  and and_19 (mulh14, comparator_3_eq, inst[25], is_R);
  and and_20 (sra5, comparator_8_eq, or_6_out);
  or or_10 (add0, is_I_load, is_I_jalr, is_S, is_UJ, is_auipc, and_9_out, is_SB, and_8_out);
  Multiplexer #(.enable("false"), .width(3)) multiplexer_1 (
    .in1(3'b100), .out(multiplexer_1_out), .sel(is_UJ));  // open: in0
  not not_2 (not_2_out, BrEq);
  not not_3 (not_3_out, BrLt);
  and and_21 (and_21_out, not_2_out, not_3_out);
  Multiplexer #(.enable("false"), .width(3)) multiplexer_2 (
    .in0(multiplexer_1_out), .in1(3'b011), .out(multiplexer_2_out), .sel(is_U));
  Comparator #(.mode("unsigned"), .width(3)) comparator_23 (.a(inst[14:12]), .b(3'b101), .gt(BrUn));  // open: eq, lt
  nor nor_1 (funct7_zero, inst[30], inst[25]);
  Multiplexer #(.enable("false"), .select(3)) multiplexer_3 (
    .in0(BrEq), .in1(not_2_out), .in4(BrLt), .in5(and_21_out), .in6(BrLt), .in7(and_21_out),
    .out(multiplexer_3_out), .sel(inst[14:12]));  // open: in2, in3
  or or_11 (RegWEn, is_R, is_I, is_U, is_UJ);
  Multiplexer #(.enable("false"), .width(3)) multiplexer_4 (
    .in0(multiplexer_2_out), .in1(3'b010), .out(multiplexer_4_out), .sel(is_SB));
  and and_22 (and_22_out, is_SB, multiplexer_3_out);
  Multiplexer #(.enable("false"), .width(3)) multiplexer_5 (
    .in0(multiplexer_4_out), .in1(3'b001), .out(multiplexer_5_out), .sel(is_S));
  or or_12 (KILL_INST, is_UJ, is_I_jalr, and_22_out);
  Multiplexer #(.enable("false"), .width(3)) multiplexer_6 (
    .in0(multiplexer_5_out), .in1(3'b000), .out(multiplexer_6_out), .sel(is_I));
  Multiplexer #(.enable("false"), .width(3)) multiplexer_7 (
    .in0(multiplexer_6_out), .in1(3'b101), .out(ImmSel), .sel(CSRWen));
  Multiplexer #(.enable("false"), .width(4)) multiplexer_8 (
    .in0(multiplexer_23_out), .in1(4'b0111), .out(multiplexer_8_out), .sel(slt7));
  not not_4 (BSel, is_R);
  Multiplexer #(.enable("false"), .width(4)) multiplexer_9 (
    .in0(4'b0000), .in1(4'b0001), .out(multiplexer_9_out), .sel(and1));
  Multiplexer #(.enable("false"), .width(4)) multiplexer_10 (
    .in0(multiplexer_8_out), .in1(4'b1010), .out(multiplexer_10_out), .sel(mul10));
  Bit_Extender #(.in_width(3), .out_width(2)) bit_extender_1 (.in(inst[14:12]), .out(bit_extender_1_out));
  nor nor_2 (ASel, is_R, is_I, is_S);
  Multiplexer #(.enable("false"), .width(4)) multiplexer_11 (
    .in0(multiplexer_9_out), .in1(4'b0010), .out(multiplexer_11_out), .sel(or2));
  Multiplexer #(.enable("false"), .width(4)) multiplexer_12 (
    .in0(multiplexer_10_out), .in1(4'b1011), .out(multiplexer_12_out), .sel(mulhu11));
  Multiplexer #(.enable("false"), .select(2), .width(4)) multiplexer_13 (
    .in0(4'b0001), .in1(4'b0011), .in2(4'b1111), .out(multiplexer_13_out), .sel(bit_extender_1_out));  // open: in3
  or or_13 (or_13_out, is_UJ, is_I_jalr);
  Bit_Extender #(.in_width(3), .out_width(2)) bit_extender_2 (.in(inst[14:12]), .out(MemR_en));
  Multiplexer #(.enable("false"), .width(4)) multiplexer_14 (
    .in0(multiplexer_11_out), .in1(4'b0011), .out(multiplexer_14_out), .sel(xor3));
  Multiplexer #(.enable("false"), .width(4)) multiplexer_15 (
    .in0(multiplexer_12_out), .in1(4'b1100), .out(multiplexer_15_out), .sel(sub12));
  Multiplexer #(.enable("false"), .width(4)) multiplexer_16 (
    .in0(4'b0000), .in1(multiplexer_13_out), .out(MemW_en), .sel(is_S));
  Multiplexer #(.enable("false"), .width(2)) multiplexer_17 (
    .in0(2'b01), .in1(2'b00), .out(multiplexer_17_out), .sel(or_13_out));
  Comparator #(.mode("unsigned"), .width(3)) comparator_24 (.a(inst[14:12]), .b(3'b101), .eq(CSRSel));  // open: gt, lt
  Multiplexer #(.enable("false"), .width(4)) multiplexer_18 (
    .in0(multiplexer_14_out), .in1(4'b0100), .out(multiplexer_18_out), .sel(srl4));
  Multiplexer #(.enable("false"), .width(4)) multiplexer_19 (
    .in0(multiplexer_15_out), .in1(4'b1101), .out(multiplexer_19_out), .sel(bsel13));
  Comparator #(.mode("unsigned"), .width(4)) comparator_25 (.a(MemW_en), .b(4'b0000), .gt(MemRW));  // open: eq, lt
  Multiplexer #(.enable("false"), .width(2)) multiplexer_20 (
    .in0(multiplexer_17_out), .in1(2'b10), .out(multiplexer_20_out), .sel(is_I_load));
  Multiplexer #(.enable("false"), .width(4)) multiplexer_21 (
    .in0(multiplexer_18_out), .in1(4'b0101), .out(multiplexer_21_out), .sel(sra5));
  Multiplexer #(.enable("false"), .width(2)) multiplexer_22 (
    .in0(multiplexer_20_out), .in1(2'b11), .out(WBSel), .sel(CSRWen));
  Multiplexer #(.enable("false"), .width(4)) multiplexer_23 (
    .in0(multiplexer_21_out), .in1(4'b0110), .out(multiplexer_23_out), .sel(sll6));
  Multiplexer #(.enable("false"), .width(4)) multiplexer_24 (
    .in0(multiplexer_19_out), .in1(4'b1110), .out(ALUSel), .sel(mulh14));

  assign PCSel = KILL_INST;

  // Other names for the same wires on the sheet: opcode[6:0] = inst[6:0]; funct3[2:0] = inst[14:12];
  //   funct7[6:0] = inst[31:25]; funct7_mul_ex = inst[25]; funct7_signed = inst[30]; is_I_csr = CSRWen;
  //   is_lui = bsel13

  // Notes on the sheet:
  //   INPUTS to your circuit
  //   DON'T CHANGE THE LOCATIONS OF THE INPUTS AND OUTPUTS!
  //   OUTPUT from your circuit
  //   RegWEn
  //   PCSel
  //   ImmSel
  //   MemW_en
  //   ALUSel
  //   WBSel
endmodule
