// Logisim project cpu.circ as structural Verilog: 1 circuit, main circuit cpu
module cpu (
  input  clk,
  input  [31:0] INSTRUCTION,
  input  [31:0] READ_DATA,
  output [31:0] WRITE_ADDRESS,
  output [31:0] PROGRAM_COUNTER,
  output [31:0] ra,
  output [31:0] sp,
  output [31:0] t0,
  output [31:0] t1,
  output [31:0] t2,
  output [31:0] s0,
  output [31:0] s1,
  output [31:0] a0,
  output [31:0] tohost,
  output [3:0] WRITE_ENABLE,
  output [31:0] WRITE_DATA
);

  wire ASel, BrEq, BrLt, BrUn, BSel, CSRSel, CSRWen, KILL_INST, PCSel, RegWEn;
  wire [1:0] MemR_en, WBSel;
  wire [2:0] Immsel;
  wire [3:0] ALUSel;
  wire [7:0] bit_extender_1_out;
  wire [15:0] bit_extender_2_out;
  wire [31:0] adder_1_out, adder_2_out, bit_extender_3_out, bit_extender_4_out, csr_din, imm, INST_ID,
       multiplexer_1_out, multiplexer_2_out, multiplexer_3_out, multiplexer_4_out, multiplexer_6_out, PC_ID,
       rs1, wb;

  Adder #(.width(32)) adder_1 (.a(PROGRAM_COUNTER), .b(32'h4), .out(adder_1_out));  // open: cin, cout
  Multiplexer #(.enable("false"), .width(32)) multiplexer_1 (
    .in0(adder_1_out), .in1(WRITE_ADDRESS), .out(multiplexer_1_out), .sel(PCSel));
  Register #(.width(32)) PC (.D(multiplexer_1_out), .clk(clk), .Q(PROGRAM_COUNTER));  // open: en, clr
  Multiplexer #(.enable("false"), .width(32)) multiplexer_2 (
    .in0(INSTRUCTION), .in1(32'h13), .out(multiplexer_2_out), .sel(KILL_INST));
  Register #(.width(32)) u_PC_ID (.D(PROGRAM_COUNTER), .clk(clk), .Q(PC_ID));  // open: en, clr
  Register #(.width(32)) u_INST_ID (.D(multiplexer_2_out), .clk(clk), .Q(INST_ID));  // open: en, clr
  control_logic control_logic_1 (
    .inst(INST_ID), .BrEq(BrEq), .BrLt(BrLt), .MemW_en(WRITE_ENABLE), .MemR_en(MemR_en),
    .KILL_INST(KILL_INST), .PCSel(PCSel), .RegWEn(RegWEn), .ImmSel(Immsel), .BrUn(BrUn), .ASel(ASel),
    .BSel(BSel), .ALUSel(ALUSel), .WBSel(WBSel), .CSRSel(CSRSel), .CSRWen(CSRWen));  // open: MemRW
  imm_gen imm_gen_1 (.inst(INST_ID), .ImmSel(Immsel), .imm(imm));
  branch_comp branch_comp_1 (.rs1(rs1), .rs2(WRITE_DATA), .BrUn(BrUn), .BrEq(BrEq), .BrLt(BrLt));
  regfile regfile_1 (
    .rs1(INST_ID[19:15]), .rs2(INST_ID[24:20]), .rd(INST_ID[11:7]), .Write_Data(wb), .RegWEn(RegWEn),
    .clk(clk), .ra(ra), .sp(sp), .t0(t0), .t1(t1), .t2(t2), .s0(s0), .s1(s1), .a0(a0), .Read_Data_1(rs1),
    .Read_Data_2(WRITE_DATA));
  Multiplexer #(.enable("false"), .width(32)) multiplexer_3 (
    .in0(rs1), .in1(PC_ID), .out(multiplexer_3_out), .sel(ASel));
  Multiplexer #(.enable("false"), .width(32)) multiplexer_4 (
    .in0(WRITE_DATA), .in1(imm), .out(multiplexer_4_out), .sel(BSel));
  Multiplexer #(.enable("false"), .width(32)) multiplexer_5 (.in0(rs1), .in1(imm), .out(csr_din), .sel(CSRSel));
  alu alu_1 (.Result(WRITE_ADDRESS), .A(multiplexer_3_out), .B(multiplexer_4_out), .ALUSel(ALUSel));
  Bit_Extender #(.in_width(32), .out_width(8)) bit_extender_1 (.in(READ_DATA), .out(bit_extender_1_out));
  Bit_Extender #(.in_width(32)) bit_extender_2 (.in(READ_DATA), .out(bit_extender_2_out));
  assign bit_extender_3_out = {{24{bit_extender_1_out[7]}}, bit_extender_1_out};  // Bit_Extender bit_extender_3
  assign bit_extender_4_out = {{16{bit_extender_2_out[15]}}, bit_extender_2_out};  // Bit_Extender bit_extender_4
  csr csr_1 (.CSR_address(INST_ID[31:20]), .CSR_din(csr_din), .CSR_WE(CSRWen), .clk(clk), .tohost(tohost));
  Adder #(.width(32)) adder_2 (.a(32'h4), .b(PC_ID), .out(adder_2_out));  // open: cin, cout
  Multiplexer #(.enable("false"), .select(2), .width(32)) multiplexer_6 (
    .in0(bit_extender_3_out), .in1(bit_extender_4_out), .in2(READ_DATA), .out(multiplexer_6_out),
    .sel(MemR_en));  // open: in3
  Multiplexer #(.enable("false"), .select(2), .width(32)) multiplexer_7 (
    .in0(adder_2_out), .in1(WRITE_ADDRESS), .in2(multiplexer_6_out), .in3(tohost), .out(wb), .sel(WBSel));

  // Other names for the same wires on the sheet: alu_ret[31:0] = WRITE_ADDRESS; MemW_en[3:0] = WRITE_ENABLE;
  //   rs2[31:0] = WRITE_DATA

  // Notes on the sheet:
  //   Output to IMEM
  //   IMEM (do **NOT** move this)
  //   Inputs from IMEM
  //   It is OK to move the PC, RegFile, ALU, MEM, Branch Comp, Imm Gen, and Control Logic to wherever is most convenient for you when constructing your CPU, and to delete this text
  //   Inputs/Outputs for testing. Do **NOT** move these.
  //   Outputs To DMEM
  //   DMEM (do **NOT** move this)
  //   Inputs From DMEM
endmodule
